# Fritzing sketch block diagram (saved by Fritzing 1.0.2b)
breadboards: 1

parts:
  Součástka1 = Arduino Nano (Rev3.0)
  Součástka2 = NRF24L01+ Breakout Board
  R1 = Rotary Potentiometer (Large) [maximum_resistance=100kΩ knob_status=50% power=0.5W package=THT]
  S1 = Pushbutton [package="[THT]"]
  LED1 = RGB LED - (4 legs) [color="Red (633nm)" current=0.030A package="5 mm [THT]"]
  Mod1 = Passive Buzzer

nets:
  GND: Součástka1.GND, Součástka2.GND, R1.leg2, S1.Pin_1, S1.Pin_2, LED1.red_cathode, Mod1.-
  N1: Součástka1.D2, LED1.common_anode
  N2: Součástka1.D3, LED1.green_cathode
  N3: Součástka1.D4, LED1.blue_cathode
  N4: Součástka1.D5, S1.Pin_3, S1.Pin_4
  N5: Součástka1.D7, Součástka2.CE
  N6: Součástka1.D8, Součástka2.CS
  N7: Součástka1.D9, Mod1.NC
  N8: Součástka1.D11/MOSI, Součástka2.MOSI
  N9: Součástka1.D12/MISO, Součástka2.MISO
  N10: Součástka1.5V, R1.leg1, Mod1.S
  N11: Součástka1.A0, R1.wiper
  3V3: Součástka1.3V3, Součástka2.VCC
  N12: Součástka1.D13/SCK, Součástka2.SCK
